# Fritzing sketch joystick_module (saved by Fritzing 0.9.9b)

parts:
  Bauteil1 = Adafruit ADS1015 12Bit I2C ADC [part_number="Adafruit #1083"]
  R1 = Resistor [tolerance=±5% power=0.25 resistance=10k package=THT]
  R2 = Trimmer Potentiometer [maximum_resistance=10kΩ package=THT]
  R3 = Trimmer Potentiometer [maximum_resistance=10kΩ package=THT]
  R4 = Trimmer Potentiometer [maximum_resistance=10kΩ package=THT]
  S1 = Pushbutton [package=THT]

nets:
  N1: Bauteil1.AIN3, R1.Pin_1, S1.leg0
  N2: Bauteil1.AIN2, R4.wiper
  N3: Bauteil1.AIN1, R2.wiper
  N4: Bauteil1.AIN0, R3.wiper
  N5: Bauteil1.ADDR, Bauteil1.GND, R1.Pin_0, R2.leg1, R3.leg1, R4.leg1
  N6: Bauteil1.VDD, R2.leg2, R3.leg2, R4.leg2, S1.leg1

notes:
  X-Axis
  Y-Axis
  Z-Axis
  Top-Button
  Connect addr pin with
  - GND for first address 0x48 (shown as example)
  - VDD for second address 0x49
  - SDA for third address 0x4A
  - SCL for fourth address 0x4B

custom parts:
  Adafruit ADS1015 12Bit I2C ADC: For microcontrollers without an analog-to-digital converter or when you want a higher-precision ADC, the ADS1015 provides 12-bit precision at 3300 samples/second over I2C. The chip can be configured as 4 single-ended input channels, or two differential channels. As a nice bonus, it even includes a programmable gain amplifier, up to x16, to help boost up smaller single/differential signals to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
